// Logisim project 9sComplement.circ as structural Verilog: 1 circuit, main circuit main
module main (
  input  in_1,
  input  in_2,
  input  in_3,
  input  in_4,
  output out_5,
  output out_6,
  output out_7,
  output out_8
);

  wire not_1_out, not_2_out, not_3_out;

  and A (out_5, not_1_out, not_2_out, not_3_out);
  xor B (out_6, in_2, in_3);
  not not_1 (not_1_out, in_1);
  not not_2 (not_2_out, in_2);
  not not_3 (not_3_out, in_3);
  not not_4 (out_8, in_4);

  assign out_7 = in_3;
endmodule
