// Logisim project CSADD.circ as structural Verilog
module main (
  input  x,
  input  y,
  input  R,
  output out_4,
  output out_5
);

  wire and_1_out, and_2_out, clock_1_out, d_ff_2_q, xor_1_out, xor_2_out, xor_3_out;

  Clock clock_1 (.out(clock_1_out));
  and and_1 (and_1_out, x, xor_2_out);
  D_Flip_Flop d_ff_1 (.D(xor_1_out), .clk(clock_1_out), .Q(out_4), .reset(R));  // open: Qn, preset
  xor xor_1 (xor_1_out, x, xor_2_out);
  xor xor_2 (xor_2_out, y, d_ff_2_q);
  and and_2 (and_2_out, y, d_ff_2_q);
  and and_3 (out_5, and_1_out, and_2_out);
  D_Flip_Flop d_ff_2 (.D(xor_3_out), .clk(clock_1_out), .Q(d_ff_2_q), .reset(R));  // open: Qn, preset
  xor xor_3 (xor_3_out, and_1_out, and_2_out);

  // Notes on the sheet:
  //   clk
  //   FDHA
  //   CAR2
  //   HSUM1
  //   CAR1
  //   SUM
  //   FDHA
endmodule

module CSADD (
  input  X,
  input  Y,
  input  R,
  input  clk,
  output sum,
  output FDHA
);

  wire and_1_out, and_2_out, d_ff_2_q, xor_1_out, xor_2_out, xor_3_out;

  and and_1 (and_1_out, X, xor_2_out);
  D_Flip_Flop d_ff_1 (.D(xor_1_out), .clk(clk), .Q(sum), .reset(R));  // open: Qn, preset
  xor xor_1 (xor_1_out, X, xor_2_out);
  xor xor_2 (xor_2_out, Y, d_ff_2_q);
  and and_2 (and_2_out, Y, d_ff_2_q);
  and and_3 (FDHA, and_1_out, and_2_out);
  D_Flip_Flop d_ff_2 (.D(xor_3_out), .clk(clk), .Q(d_ff_2_q), .reset(R));  // open: Qn, preset
  xor xor_3 (xor_3_out, and_1_out, and_2_out);

  // Notes on the sheet:
  //   x
  //   y
  //   R
  //   FDHA
  //   CAR2
  //   HSUM1
  //   CAR1
  //   SUM
  //   FDHA
endmodule
