// Logisim project comparativeAdder.circ as structural Verilog: 1 circuit, main circuit main
module main (
  input  in0,
  input  in1,
  input  in2,
  input  in3,
  output O0,
  output O1,
  output O2,
  output O3
);

  wire and_1_out, and_2_out, and_3_out, and_4_out, and_5_out, or_1_out, or_2_out, xor_2_out, xor_3_out,
       xor_4_out;

  xor xor_1 (O0, 1'b1, in0);
  and and_1 (and_1_out, 1'b1, in0);
  xor xor_2 (xor_2_out, 1'b1, in1);
  and and_2 (and_2_out, 1'b1, in1);
  xor xor_3 (xor_3_out, in2, 1'b0);
  and and_3 (and_3_out, in2, 1'b0);
  xor xor_4 (xor_4_out, in3, 1'b0);
  // Probe on O0
  and and_4 (and_4_out, and_1_out, xor_2_out);
  // Probe on O1
  xor xor_5 (O1, and_1_out, xor_2_out);
  or or_1 (or_1_out, and_4_out, and_2_out);
  xor xor_6 (O2, or_1_out, xor_3_out);
  and and_5 (and_5_out, or_1_out, xor_3_out);
  // Probe on O2
  or or_2 (or_2_out, and_5_out, and_3_out);
  xor xor_7 (O3, or_2_out, xor_4_out);
  // Probe on O3
endmodule
