// Logisim project comparator4bit.circ as structural Verilog: 1 circuit, main circuit main
module main (
  input  I3,
  input  I2,
  input  I1,
  input  I0,
  output O
);

  wire and_1_out, and_2_out, and_3_out, and_4_out, not_1_out, not_2_out, not_3_out, not_4_out, xnor_1_out,
       xnor_2_out, xnor_3_out;

  not not_1 (not_1_out, 1'b0);
  not not_2 (not_2_out, 1'b1);
  not not_3 (not_3_out, 1'b0);
  not not_4 (not_4_out, 1'b0);
  and and_1 (and_1_out, not_1_out, I3);
  xnor xnor_1 (xnor_1_out, 1'b1, I2);
  xnor xnor_2 (xnor_2_out, 1'b0, I3);
  xnor xnor_3 (xnor_3_out, 1'b0, I1);
  and and_2 (and_2_out, xnor_2_out, xnor_1_out, not_3_out, I1);
  and and_3 (and_3_out, xnor_2_out, xnor_1_out, xnor_3_out, I0, not_4_out);
  and and_4 (and_4_out, xnor_2_out, not_2_out, I2);
  or or_1 (O, and_1_out, and_4_out, and_2_out, and_3_out);
  // Probe on O
endmodule
