// Logisim project double.circ as structural Verilog: 4 circuits, main circuit adder4bit
module adder4bit (
  input  in0,
  input  in1,
  input  in2,
  input  in3,
  output O0,
  output O1,
  output O2,
  output O3
);

  wire and_1_out, and_2_out, and_3_out, and_4_out, and_5_out, or_1_out, or_2_out, xor_2_out, xor_3_out,
       xor_4_out;

  xor xor_1 (O0, 1'b1, in0);
  and and_1 (and_1_out, 1'b1, in0);
  xor xor_2 (xor_2_out, 1'b1, in1);
  and and_2 (and_2_out, 1'b1, in1);
  xor xor_3 (xor_3_out, in2, 1'b0);
  and and_3 (and_3_out, in2, 1'b0);
  xor xor_4 (xor_4_out, in3, 1'b0);
  // Probe on O0
  and and_4 (and_4_out, and_1_out, xor_2_out);
  // Probe on O1
  xor xor_5 (O1, and_1_out, xor_2_out);
  or or_1 (or_1_out, and_4_out, and_2_out);
  xor xor_6 (O2, or_1_out, xor_3_out);
  and and_5 (and_5_out, or_1_out, xor_3_out);
  // Probe on O2
  or or_2 (or_2_out, and_5_out, and_3_out);
  xor xor_7 (O3, or_2_out, xor_4_out);
  // Probe on O3
endmodule

module comparator4bit (
  input  I3,
  input  I2,
  input  I1,
  input  I0,
  output O
);

  wire and_1_out, and_2_out, and_3_out, and_4_out, not_1_out, not_2_out, not_3_out, not_4_out, xnor_1_out,
       xnor_2_out, xnor_3_out;

  not not_1 (not_1_out, 1'b0);
  not not_2 (not_2_out, 1'b1);
  not not_3 (not_3_out, 1'b0);
  not not_4 (not_4_out, 1'b0);
  and and_1 (and_1_out, not_1_out, I3);
  xnor xnor_1 (xnor_1_out, 1'b1, I2);
  xnor xnor_2 (xnor_2_out, 1'b0, I3);
  xnor xnor_3 (xnor_3_out, 1'b0, I1);
  and and_2 (and_2_out, xnor_2_out, xnor_1_out, not_3_out, I1);
  and and_3 (and_3_out, xnor_2_out, xnor_1_out, xnor_3_out, I0, not_4_out);
  and and_4 (and_4_out, xnor_2_out, not_2_out, I2);
  or or_1 (O, and_1_out, and_4_out, and_2_out, and_3_out);
  // Probe on O
endmodule

module comparativeAdder (
  input  I0,
  input  I1,
  input  I2,
  input  I3,
  output O0,
  output O1,
  output O2,
  output O3
);

  wire comparator4bit_1_o;
  wire [3:0] adder4bit_1_o0;

  adder4bit adder4bit_1 (
    .in0(I0), .in1(I1), .in2(I2), .in3(I3), .O0(adder4bit_1_o0[0]), .O1(adder4bit_1_o0[1]),
    .O2(adder4bit_1_o0[2]), .O3(adder4bit_1_o0[3]));
  comparator4bit comparator4bit_1 (.I3(I3), .I2(I2), .I1(I1), .I0(I0), .O(comparator4bit_1_o));
  Multiplexer #(.width(4)) multiplexer_1 (
    .in0({I3, I2, I1, I0}), .in1(adder4bit_1_o0), .out({O3, O2, O1, O0}), .sel(comparator4bit_1_o));
  // Probe on O0
  // Probe on O1
  // Probe on O2
  // Probe on O3
endmodule

module doubleDabble (
  input  [15:0] in_1
);

  wire comparativeadder_1_o0, comparativeadder_1_o1, comparativeadder_1_o2, comparativeadder_1_o3,
       comparativeadder_2_o0, comparativeadder_2_o1, comparativeadder_2_o2, comparativeadder_2_o3,
       comparativeadder_3_o0, comparativeadder_3_o1, comparativeadder_3_o2, comparativeadder_3_o3,
       comparativeadder_4_o0, comparativeadder_4_o1, comparativeadder_4_o2, comparativeadder_4_o3,
       comparativeadder_5_o0, comparativeadder_5_o1, comparativeadder_5_o2, comparativeadder_5_o3,
       comparativeadder_6_o0, comparativeadder_6_o1, comparativeadder_6_o2, comparativeadder_6_o3,
       comparativeadder_7_o0, comparativeadder_7_o1, comparativeadder_7_o2, comparativeadder_7_o3,
       comparativeadder_8_o0, comparativeadder_8_o1, comparativeadder_8_o2, comparativeadder_8_o3,
       comparativeadder_9_o0, comparativeadder_9_o1, comparativeadder_9_o2, comparativeadder_9_o3,
       comparativeadder_10_o0, comparativeadder_10_o1, comparativeadder_10_o2, comparativeadder_10_o3,
       comparativeadder_11_o0, comparativeadder_11_o1, comparativeadder_11_o2, comparativeadder_11_o3,
       comparativeadder_12_o0, comparativeadder_12_o1, comparativeadder_12_o2, comparativeadder_12_o3,
       comparativeadder_13_o0, comparativeadder_13_o1, comparativeadder_13_o2, comparativeadder_13_o3,
       comparativeadder_14_o0, comparativeadder_14_o1, comparativeadder_14_o2, comparativeadder_14_o3,
       comparativeadder_15_o0, comparativeadder_15_o1, comparativeadder_15_o2, comparativeadder_15_o3,
       comparativeadder_16_o0, comparativeadder_16_o1, comparativeadder_16_o2, comparativeadder_16_o3,
       comparativeadder_17_o0, comparativeadder_17_o1, comparativeadder_17_o2, comparativeadder_17_o3,
       comparativeadder_18_o0, comparativeadder_18_o1, comparativeadder_18_o2, comparativeadder_18_o3,
       comparativeadder_19_o0, comparativeadder_19_o1, comparativeadder_19_o2, comparativeadder_19_o3,
       comparativeadder_20_o0, comparativeadder_20_o1, comparativeadder_20_o2, comparativeadder_20_o3,
       comparativeadder_21_o0, comparativeadder_21_o1, comparativeadder_21_o2, comparativeadder_21_o3,
       comparativeadder_22_o0, comparativeadder_22_o1, comparativeadder_22_o2, comparativeadder_22_o3,
       comparativeadder_23_o0, comparativeadder_23_o1, comparativeadder_23_o2, comparativeadder_23_o3,
       comparativeadder_24_o0, comparativeadder_24_o1, comparativeadder_24_o2, comparativeadder_24_o3,
       comparativeadder_25_o0, comparativeadder_25_o1, comparativeadder_25_o2, comparativeadder_25_o3,
       comparativeadder_26_o0, comparativeadder_26_o1, comparativeadder_26_o2, comparativeadder_26_o3,
       comparativeadder_27_o0, comparativeadder_27_o1, comparativeadder_27_o2, comparativeadder_27_o3,
       comparativeadder_28_o0, comparativeadder_28_o1, comparativeadder_28_o2, comparativeadder_28_o3,
       comparativeadder_29_o0, comparativeadder_29_o1, comparativeadder_29_o2, comparativeadder_29_o3,
       comparativeadder_30_o0, comparativeadder_30_o1, comparativeadder_30_o2, comparativeadder_30_o3;
  wire [0:0] comparativeadder_35_o3;
  wire [3:0] comparativeadder_31_o3, comparativeadder_32_o3, comparativeadder_33_o3, comparativeadder_34_o3;
  wire [3:1] comparativeadder_31_o0;

  comparativeAdder comparativeadder_1 (
    .I0(in_1[13]), .I1(in_1[14]), .I2(in_1[15]), .I3(1'b0), .O0(comparativeadder_1_o0),
    .O1(comparativeadder_1_o1), .O2(comparativeadder_1_o2), .O3(comparativeadder_1_o3));
  comparativeAdder comparativeadder_2 (
    .I0(in_1[12]), .I1(comparativeadder_1_o0), .I2(comparativeadder_1_o1), .I3(comparativeadder_1_o2),
    .O0(comparativeadder_2_o0), .O1(comparativeadder_2_o1), .O2(comparativeadder_2_o2),
    .O3(comparativeadder_2_o3));
  comparativeAdder comparativeadder_3 (
    .I0(in_1[11]), .I1(comparativeadder_2_o0), .I2(comparativeadder_2_o1), .I3(comparativeadder_2_o2),
    .O0(comparativeadder_3_o0), .O1(comparativeadder_3_o1), .O2(comparativeadder_3_o2),
    .O3(comparativeadder_3_o3));
  comparativeAdder comparativeadder_4 (
    .I0(in_1[10]), .I1(comparativeadder_3_o0), .I2(comparativeadder_3_o1), .I3(comparativeadder_3_o2),
    .O0(comparativeadder_4_o0), .O1(comparativeadder_4_o1), .O2(comparativeadder_4_o2),
    .O3(comparativeadder_4_o3));
  comparativeAdder comparativeadder_5 (
    .I0(comparativeadder_3_o3), .I1(comparativeadder_2_o3), .I2(comparativeadder_1_o3), .I3(1'b0),
    .O0(comparativeadder_5_o0), .O1(comparativeadder_5_o1), .O2(comparativeadder_5_o2),
    .O3(comparativeadder_5_o3));
  comparativeAdder comparativeadder_6 (
    .I0(in_1[9]), .I1(comparativeadder_4_o0), .I2(comparativeadder_4_o1), .I3(comparativeadder_4_o2),
    .O0(comparativeadder_6_o0), .O1(comparativeadder_6_o1), .O2(comparativeadder_6_o2),
    .O3(comparativeadder_6_o3));
  comparativeAdder comparativeadder_7 (
    .I0(comparativeadder_4_o3), .I1(comparativeadder_5_o0), .I2(comparativeadder_5_o1),
    .I3(comparativeadder_5_o2), .O0(comparativeadder_7_o0), .O1(comparativeadder_7_o1),
    .O2(comparativeadder_7_o2), .O3(comparativeadder_7_o3));
  comparativeAdder comparativeadder_8 (
    .I0(in_1[8]), .I1(comparativeadder_6_o0), .I2(comparativeadder_6_o1), .I3(comparativeadder_6_o2),
    .O0(comparativeadder_8_o0), .O1(comparativeadder_8_o1), .O2(comparativeadder_8_o2),
    .O3(comparativeadder_8_o3));
  comparativeAdder comparativeadder_9 (
    .I0(comparativeadder_6_o3), .I1(comparativeadder_7_o0), .I2(comparativeadder_7_o1),
    .I3(comparativeadder_7_o2), .O0(comparativeadder_9_o0), .O1(comparativeadder_9_o1),
    .O2(comparativeadder_9_o2), .O3(comparativeadder_9_o3));
  comparativeAdder comparativeadder_10 (
    .I0(in_1[7]), .I1(comparativeadder_8_o0), .I2(comparativeadder_8_o1), .I3(comparativeadder_8_o2),
    .O0(comparativeadder_10_o0), .O1(comparativeadder_10_o1), .O2(comparativeadder_10_o2),
    .O3(comparativeadder_10_o3));
  comparativeAdder comparativeadder_11 (
    .I0(comparativeadder_8_o3), .I1(comparativeadder_9_o0), .I2(comparativeadder_9_o1),
    .I3(comparativeadder_9_o2), .O0(comparativeadder_11_o0), .O1(comparativeadder_11_o1),
    .O2(comparativeadder_11_o2), .O3(comparativeadder_11_o3));
  comparativeAdder comparativeadder_12 (
    .I0(comparativeadder_9_o3), .I1(comparativeadder_7_o3), .I2(comparativeadder_5_o3), .I3(1'b0),
    .O0(comparativeadder_12_o0), .O1(comparativeadder_12_o1), .O2(comparativeadder_12_o2),
    .O3(comparativeadder_12_o3));
  comparativeAdder comparativeadder_13 (
    .I0(in_1[6]), .I1(comparativeadder_10_o0), .I2(comparativeadder_10_o1), .I3(comparativeadder_10_o2),
    .O0(comparativeadder_13_o0), .O1(comparativeadder_13_o1), .O2(comparativeadder_13_o2),
    .O3(comparativeadder_13_o3));
  comparativeAdder comparativeadder_14 (
    .I0(comparativeadder_10_o3), .I1(comparativeadder_11_o0), .I2(comparativeadder_11_o1),
    .I3(comparativeadder_11_o2), .O0(comparativeadder_14_o0), .O1(comparativeadder_14_o1),
    .O2(comparativeadder_14_o2), .O3(comparativeadder_14_o3));
  comparativeAdder comparativeadder_15 (
    .I0(comparativeadder_11_o3), .I1(comparativeadder_12_o0), .I2(comparativeadder_12_o1),
    .I3(comparativeadder_12_o2), .O0(comparativeadder_15_o0), .O1(comparativeadder_15_o1),
    .O2(comparativeadder_15_o2), .O3(comparativeadder_15_o3));
  comparativeAdder comparativeadder_16 (
    .I0(in_1[5]), .I1(comparativeadder_13_o0), .I2(comparativeadder_13_o1), .I3(comparativeadder_13_o2),
    .O0(comparativeadder_16_o0), .O1(comparativeadder_16_o1), .O2(comparativeadder_16_o2),
    .O3(comparativeadder_16_o3));
  comparativeAdder comparativeadder_17 (
    .I0(comparativeadder_13_o3), .I1(comparativeadder_14_o0), .I2(comparativeadder_14_o1),
    .I3(comparativeadder_14_o2), .O0(comparativeadder_17_o0), .O1(comparativeadder_17_o1),
    .O2(comparativeadder_17_o2), .O3(comparativeadder_17_o3));
  comparativeAdder comparativeadder_18 (
    .I0(comparativeadder_14_o3), .I1(comparativeadder_15_o0), .I2(comparativeadder_15_o1),
    .I3(comparativeadder_15_o2), .O0(comparativeadder_18_o0), .O1(comparativeadder_18_o1),
    .O2(comparativeadder_18_o2), .O3(comparativeadder_18_o3));
  comparativeAdder comparativeadder_19 (
    .I0(in_1[4]), .I1(comparativeadder_16_o0), .I2(comparativeadder_16_o1), .I3(comparativeadder_16_o2),
    .O0(comparativeadder_19_o0), .O1(comparativeadder_19_o1), .O2(comparativeadder_19_o2),
    .O3(comparativeadder_19_o3));
  comparativeAdder comparativeadder_20 (
    .I0(comparativeadder_16_o3), .I1(comparativeadder_17_o0), .I2(comparativeadder_17_o1),
    .I3(comparativeadder_17_o2), .O0(comparativeadder_20_o0), .O1(comparativeadder_20_o1),
    .O2(comparativeadder_20_o2), .O3(comparativeadder_20_o3));
  comparativeAdder comparativeadder_21 (
    .I0(comparativeadder_17_o3), .I1(comparativeadder_18_o0), .I2(comparativeadder_18_o1),
    .I3(comparativeadder_18_o2), .O0(comparativeadder_21_o0), .O1(comparativeadder_21_o1),
    .O2(comparativeadder_21_o2), .O3(comparativeadder_21_o3));
  comparativeAdder comparativeadder_22 (
    .I0(comparativeadder_18_o3), .I1(comparativeadder_15_o3), .I2(comparativeadder_12_o3), .I3(1'b0),
    .O0(comparativeadder_22_o0), .O1(comparativeadder_22_o1), .O2(comparativeadder_22_o2),
    .O3(comparativeadder_22_o3));
  comparativeAdder comparativeadder_23 (
    .I0(in_1[3]), .I1(comparativeadder_19_o0), .I2(comparativeadder_19_o1), .I3(comparativeadder_19_o2),
    .O0(comparativeadder_23_o0), .O1(comparativeadder_23_o1), .O2(comparativeadder_23_o2),
    .O3(comparativeadder_23_o3));
  comparativeAdder comparativeadder_24 (
    .I0(comparativeadder_19_o3), .I1(comparativeadder_20_o0), .I2(comparativeadder_20_o1),
    .I3(comparativeadder_20_o2), .O0(comparativeadder_24_o0), .O1(comparativeadder_24_o1),
    .O2(comparativeadder_24_o2), .O3(comparativeadder_24_o3));
  comparativeAdder comparativeadder_25 (
    .I0(comparativeadder_20_o3), .I1(comparativeadder_21_o0), .I2(comparativeadder_21_o1),
    .I3(comparativeadder_21_o2), .O0(comparativeadder_25_o0), .O1(comparativeadder_25_o1),
    .O2(comparativeadder_25_o2), .O3(comparativeadder_25_o3));
  comparativeAdder comparativeadder_26 (
    .I0(comparativeadder_21_o3), .I1(comparativeadder_22_o0), .I2(comparativeadder_22_o1),
    .I3(comparativeadder_22_o2), .O0(comparativeadder_26_o0), .O1(comparativeadder_26_o1),
    .O2(comparativeadder_26_o2), .O3(comparativeadder_26_o3));
  comparativeAdder comparativeadder_27 (
    .I0(in_1[2]), .I1(comparativeadder_23_o0), .I2(comparativeadder_23_o1), .I3(comparativeadder_23_o2),
    .O0(comparativeadder_27_o0), .O1(comparativeadder_27_o1), .O2(comparativeadder_27_o2),
    .O3(comparativeadder_27_o3));
  comparativeAdder comparativeadder_28 (
    .I0(comparativeadder_23_o3), .I1(comparativeadder_24_o0), .I2(comparativeadder_24_o1),
    .I3(comparativeadder_24_o2), .O0(comparativeadder_28_o0), .O1(comparativeadder_28_o1),
    .O2(comparativeadder_28_o2), .O3(comparativeadder_28_o3));
  comparativeAdder comparativeadder_29 (
    .I0(comparativeadder_24_o3), .I1(comparativeadder_25_o0), .I2(comparativeadder_25_o1),
    .I3(comparativeadder_25_o2), .O0(comparativeadder_29_o0), .O1(comparativeadder_29_o1),
    .O2(comparativeadder_29_o2), .O3(comparativeadder_29_o3));
  comparativeAdder comparativeadder_30 (
    .I0(comparativeadder_25_o3), .I1(comparativeadder_26_o0), .I2(comparativeadder_26_o1),
    .I3(comparativeadder_26_o2), .O0(comparativeadder_30_o0), .O1(comparativeadder_30_o1),
    .O2(comparativeadder_30_o2), .O3(comparativeadder_30_o3));
  comparativeAdder comparativeadder_31 (
    .I0(in_1[1]), .I1(comparativeadder_27_o0), .I2(comparativeadder_27_o1), .I3(comparativeadder_27_o2),
    .O0(comparativeadder_31_o0[1]), .O1(comparativeadder_31_o0[2]), .O2(comparativeadder_31_o0[3]),
    .O3(comparativeadder_31_o3[0]));
  comparativeAdder comparativeadder_32 (
    .I0(comparativeadder_27_o3), .I1(comparativeadder_28_o0), .I2(comparativeadder_28_o1),
    .I3(comparativeadder_28_o2), .O0(comparativeadder_31_o3[1]), .O1(comparativeadder_31_o3[2]),
    .O2(comparativeadder_31_o3[3]), .O3(comparativeadder_32_o3[0]));
  comparativeAdder comparativeadder_33 (
    .I0(comparativeadder_28_o3), .I1(comparativeadder_29_o0), .I2(comparativeadder_29_o1),
    .I3(comparativeadder_29_o2), .O0(comparativeadder_32_o3[1]), .O1(comparativeadder_32_o3[2]),
    .O2(comparativeadder_32_o3[3]), .O3(comparativeadder_33_o3[0]));
  comparativeAdder comparativeadder_34 (
    .I0(comparativeadder_29_o3), .I1(comparativeadder_30_o0), .I2(comparativeadder_30_o1),
    .I3(comparativeadder_30_o2), .O0(comparativeadder_33_o3[1]), .O1(comparativeadder_33_o3[2]),
    .O2(comparativeadder_33_o3[3]), .O3(comparativeadder_34_o3[0]));
  comparativeAdder comparativeadder_35 (
    .I0(comparativeadder_30_o3), .I1(comparativeadder_26_o3), .I2(comparativeadder_22_o3), .I3(1'b0),
    .O0(comparativeadder_34_o3[1]), .O1(comparativeadder_34_o3[2]), .O2(comparativeadder_34_o3[3]),
    .O3(comparativeadder_35_o3[0]));
  // Probe on comparativeadder_31_o3
  // Probe on comparativeadder_33_o3
  // Probe on comparativeadder_34_o3
  // Probe on {3'b000, comparativeadder_35_o3[0]}
  // Probe on {comparativeadder_31_o0, in_1[0]}
  // Probe on comparativeadder_32_o3
endmodule
