// Logisim project mul.circ as structural Verilog: 4 circuits, main circuit main
module main (
  input  [7:0] X,
  input  in_2,
  input  R,
  output [15:0] out_4,
  output [15:0] out_5
);

  wire and_1_out, and_2_out, and_3_out, and_4_out, and_5_out, and_6_out, and_7_out, and_8_out, button_1_out,
       button_2_out, ciso_1_out_3, clk_out, csadd_1_sum, csadd_2_sum, csadd_3_sum, csadd_4_sum, csadd_5_sum,
       csadd_6_sum, csadd_7_sum, l_7_segment_display_driver_9440213f_1_p5,
       l_7_segment_display_driver_9440213f_1_p6, l_7_segment_display_driver_9440213f_1_p7,
       l_7_segment_display_driver_9440213f_1_p8, l_7_segment_display_driver_9440213f_1_p9,
       l_7_segment_display_driver_9440213f_1_p10, l_7_segment_display_driver_9440213f_1_p11,
       l_7_segment_display_driver_9440213f_2_p5, l_7_segment_display_driver_9440213f_2_p6,
       l_7_segment_display_driver_9440213f_2_p7, l_7_segment_display_driver_9440213f_2_p8,
       l_7_segment_display_driver_9440213f_2_p9, l_7_segment_display_driver_9440213f_2_p10,
       l_7_segment_display_driver_9440213f_2_p11, l_7_segment_display_driver_9440213f_3_p1,
       l_7_segment_display_driver_9440213f_3_p6, l_7_segment_display_driver_9440213f_3_p7,
       l_7_segment_display_driver_9440213f_3_p8, l_7_segment_display_driver_9440213f_3_p9,
       l_7_segment_display_driver_9440213f_3_p10, l_7_segment_display_driver_9440213f_3_p11,
       l_7_segment_display_driver_9440213f_3_p12, loader_1_done, main_1_out_5, multiplexer_5_out, not_1_out,
       or_1_out, or_2_out;
  wire [1:0] counter_1_q;
  wire [3:0] doubledabble_1_hundreds, doubledabble_1_ones, doubledabble_1_tens, doubledabble_1_tenthousands,
       doubledabble_1_thousands, multiplexer_2_out, multiplexer_3_out, multiplexer_4_out;
  wire [15:0] subtractor_1_out;

  Clock clk (.out(clk_out));
  ciso ciso_1 (.SI(in_2), .CLK(clk_out), .out_3(ciso_1_out_3));
  and and_1 (and_1_out, ciso_1_out_3, X[7]);
  theTCMP_main main_1 (.A(and_1_out), .R(R), .out_5(main_1_out_5), .in_2(clk_out));  // open: out_4
  Multiplexer #(.width(16)) multiplexer_1 (.in0(out_4), .in1(subtractor_1_out), .out(out_5), .sel(out_4[15]));
  and and_2 (and_2_out, ciso_1_out_3, X[6]);
  Subtractor #(.width(16)) subtractor_1 (.a({16{1'b0}}), .b(out_4), .out(subtractor_1_out));  // open: bin, bout
  CSADD csadd_1 (.Y(and_2_out), .X(main_1_out_5), .R(R), .sum(csadd_1_sum), .clk(clk_out));  // open: FDHA
  and and_3 (and_3_out, ciso_1_out_3, X[5]);
  doubleDabble doubledabble_1 (
    .Binary(out_5), .ones(doubledabble_1_ones), .tens(doubledabble_1_tens),
    .hundreds(doubledabble_1_hundreds), .thousands(doubledabble_1_thousands),
    .tenThousands(doubledabble_1_tenthousands));  // open: hundredThousands
  not not_1 (not_1_out, button_2_out);
  Button button_1 (.out(button_1_out));
  and and_4 (and_4_out, ciso_1_out_3, X[4]);
  CSADD csadd_2 (.Y(and_3_out), .X(csadd_1_sum), .R(R), .sum(csadd_2_sum), .clk(clk_out));  // open: FDHA
  Counter #(.max('h2), .width(2)) counter_1 (
    .clr(R), .up(or_1_out), .count(or_2_out), .clk(clk_out), .Q(counter_1_q));  // open: load, D, carry
  or or_1 (or_1_out, not_1_out, button_1_out);
  or or_2 (or_2_out, button_1_out, button_2_out);
  and and_5 (and_5_out, ciso_1_out_3, X[3]);
  Multiplexer #(.select(2), .width(4)) multiplexer_2 (
    .in0(doubledabble_1_ones), .in1(doubledabble_1_tens), .in2(doubledabble_1_hundreds),
    .out(multiplexer_2_out), .sel(counter_1_q));  // open: in3
  and and_6 (and_6_out, ciso_1_out_3, X[2]);
  CSADD csadd_3 (.Y(and_4_out), .X(csadd_2_sum), .R(R), .sum(csadd_3_sum), .clk(clk_out));  // open: FDHA
  and and_7 (and_7_out, ciso_1_out_3, X[1]);
  Multiplexer #(.select(2), .width(4)) multiplexer_3 (
    .in0(doubledabble_1_tens), .in1(doubledabble_1_hundreds), .in2(doubledabble_1_thousands),
    .out(multiplexer_3_out), .sel(counter_1_q));  // open: in3
  and and_8 (and_8_out, ciso_1_out_3, X[0]);
  CSADD csadd_4 (.Y(and_5_out), .X(csadd_3_sum), .R(R), .sum(csadd_4_sum), .clk(clk_out));  // open: FDHA
  Multiplexer #(.select(2), .width(4)) multiplexer_4 (
    .in0(doubledabble_1_hundreds), .in1(doubledabble_1_thousands), .in2(doubledabble_1_tenthousands),
    .out(multiplexer_4_out), .sel(counter_1_q));  // open: in3
  Button button_2 (.out(button_2_out));
  CSADD csadd_5 (.Y(and_6_out), .X(csadd_4_sum), .R(R), .sum(csadd_5_sum), .clk(clk_out));  // open: FDHA
  // L_7_segment_display_driver_9440213f l_7_segment_display_driver_9440213f_1: pin names not known; wires that end beside it: multiplexer_2_out[3], multiplexer_2_out[2], multiplexer_2_out[1], multiplexer_2_out[0], l_7_segment_display_driver_9440213f_1_p5, l_7_segment_display_driver_9440213f_1_p6, l_7_segment_display_driver_9440213f_1_p7, l_7_segment_display_driver_9440213f_1_p8, l_7_segment_display_driver_9440213f_1_p9, l_7_segment_display_driver_9440213f_1_p10, l_7_segment_display_driver_9440213f_1_p11
  Multiplexer multiplexer_5 (.in0(1'b0), .in1(1'b1), .out(multiplexer_5_out), .sel(out_4[15]));
  CSADD csadd_6 (.Y(and_7_out), .X(csadd_5_sum), .R(R), .sum(csadd_6_sum), .clk(clk_out));  // open: FDHA
  _7_Segment_Display u_7_segment_display_1 (
    .g(l_7_segment_display_driver_9440213f_1_p11), .f(l_7_segment_display_driver_9440213f_1_p10),
    .a(l_7_segment_display_driver_9440213f_1_p5), .b(l_7_segment_display_driver_9440213f_1_p6),
    .e(l_7_segment_display_driver_9440213f_1_p9), .d(l_7_segment_display_driver_9440213f_1_p8),
    .c(l_7_segment_display_driver_9440213f_1_p7));  // open: dp
  // L_7_segment_display_driver_9440213f l_7_segment_display_driver_9440213f_2: pin names not known; wires that end beside it: multiplexer_3_out[3], multiplexer_3_out[2], multiplexer_3_out[1], multiplexer_3_out[0], l_7_segment_display_driver_9440213f_2_p5, l_7_segment_display_driver_9440213f_2_p6, l_7_segment_display_driver_9440213f_2_p7, l_7_segment_display_driver_9440213f_2_p8, l_7_segment_display_driver_9440213f_2_p9, l_7_segment_display_driver_9440213f_2_p10, l_7_segment_display_driver_9440213f_2_p11
  _7_Segment_Display u_7_segment_display_2 (
    .g(l_7_segment_display_driver_9440213f_2_p11), .f(l_7_segment_display_driver_9440213f_2_p10),
    .a(l_7_segment_display_driver_9440213f_2_p5), .b(l_7_segment_display_driver_9440213f_2_p6),
    .e(l_7_segment_display_driver_9440213f_2_p9), .d(l_7_segment_display_driver_9440213f_2_p8),
    .c(l_7_segment_display_driver_9440213f_2_p7));  // open: dp
  // L_7_segment_display_driver_9440213f l_7_segment_display_driver_9440213f_3: pin names not known; wires that end beside it: l_7_segment_display_driver_9440213f_3_p1, multiplexer_4_out[3], multiplexer_4_out[2], multiplexer_4_out[1], multiplexer_4_out[0], l_7_segment_display_driver_9440213f_3_p6, l_7_segment_display_driver_9440213f_3_p7, l_7_segment_display_driver_9440213f_3_p8, l_7_segment_display_driver_9440213f_3_p9, l_7_segment_display_driver_9440213f_3_p10, l_7_segment_display_driver_9440213f_3_p11, l_7_segment_display_driver_9440213f_3_p12, l_7_segment_display_driver_9440213f_3_p1
  _7_Segment_Display u_7_segment_display_3 (
    .g(multiplexer_5_out), .f(1'b0), .a(1'b0), .e(1'b0), .d(1'b0), .c(1'b0));  // open: b, dp
  CSADD csadd_7 (.Y(and_8_out), .X(csadd_6_sum), .R(R), .sum(csadd_7_sum), .clk(clk_out));  // open: FDHA
  _7_Segment_Display u_7_segment_display_4 (
    .g(l_7_segment_display_driver_9440213f_3_p12), .f(l_7_segment_display_driver_9440213f_3_p11),
    .a(l_7_segment_display_driver_9440213f_3_p6), .b(l_7_segment_display_driver_9440213f_3_p7),
    .e(l_7_segment_display_driver_9440213f_3_p10), .d(l_7_segment_display_driver_9440213f_3_p9),
    .c(l_7_segment_display_driver_9440213f_3_p8));  // open: dp
  loader loader_1 (.rst(R), .serialIn(csadd_7_sum), .clk(clk_out), .DONE(loader_1_done), .parallelOut(out_4));
endmodule

module ciso (
  input  SI,
  input  CLK,
  output out_3
);

  wire d_ff_1_q, d_ff_2_q, d_ff_3_q, d_ff_4_q, d_ff_5_q, d_ff_6_q, d_ff_7_q;

  D_Flip_Flop d_ff_1 (.D(SI), .clk(CLK), .Q(d_ff_1_q));  // open: Qn, preset, reset
  D_Flip_Flop d_ff_2 (.D(d_ff_1_q), .clk(CLK), .Q(d_ff_2_q));  // open: Qn, preset, reset
  D_Flip_Flop d_ff_3 (.D(d_ff_2_q), .clk(CLK), .Q(d_ff_3_q));  // open: Qn, preset, reset
  D_Flip_Flop d_ff_4 (.D(d_ff_3_q), .clk(CLK), .Q(d_ff_4_q));  // open: Qn, preset, reset
  D_Flip_Flop d_ff_5 (.D(d_ff_4_q), .clk(CLK), .Q(d_ff_5_q));  // open: Qn, preset, reset
  D_Flip_Flop d_ff_6 (.D(d_ff_5_q), .clk(CLK), .Q(d_ff_6_q));  // open: Qn, preset, reset
  D_Flip_Flop d_ff_7 (.D(d_ff_6_q), .clk(CLK), .Q(d_ff_7_q));  // open: Qn, preset, reset
  D_Flip_Flop d_ff_8 (.D(d_ff_7_q), .clk(CLK), .Q(out_3));  // open: Qn, preset, reset
endmodule

module sipo (
  input  SI,
  input  CLK,
  output [15:0] product
);

  D_Flip_Flop d_ff_1 (.D(SI), .clk(CLK), .Q(product[15]));  // open: Qn, preset, reset
  D_Flip_Flop d_ff_2 (.D(product[15]), .clk(CLK), .Q(product[14]));  // open: Qn, preset, reset
  D_Flip_Flop d_ff_3 (.D(product[14]), .clk(CLK), .Q(product[13]));  // open: Qn, preset, reset
  D_Flip_Flop d_ff_4 (.D(product[13]), .clk(CLK), .Q(product[12]));  // open: Qn, preset, reset
  D_Flip_Flop d_ff_5 (.D(product[12]), .clk(CLK), .Q(product[11]));  // open: Qn, preset, reset
  D_Flip_Flop d_ff_6 (.D(product[11]), .clk(CLK), .Q(product[10]));  // open: Qn, preset, reset
  D_Flip_Flop d_ff_7 (.D(product[10]), .clk(CLK), .Q(product[9]));  // open: Qn, preset, reset
  D_Flip_Flop d_ff_8 (.D(product[9]), .clk(CLK), .Q(product[8]));  // open: Qn, preset, reset
  D_Flip_Flop d_ff_9 (.D(product[8]), .clk(CLK), .Q(product[7]));  // open: Qn, preset, reset
  D_Flip_Flop d_ff_10 (.D(product[7]), .clk(CLK), .Q(product[6]));  // open: Qn, preset, reset
  D_Flip_Flop d_ff_11 (.D(product[6]), .clk(CLK), .Q(product[5]));  // open: Qn, preset, reset
  D_Flip_Flop d_ff_12 (.D(product[5]), .clk(CLK), .Q(product[4]));  // open: Qn, preset, reset
  D_Flip_Flop d_ff_13 (.D(product[4]), .clk(CLK), .Q(product[3]));  // open: Qn, preset, reset
  D_Flip_Flop d_ff_14 (.D(product[3]), .clk(CLK), .Q(product[2]));  // open: Qn, preset, reset
  D_Flip_Flop d_ff_15 (.D(product[2]), .clk(CLK), .Q(product[1]));  // open: Qn, preset, reset
  D_Flip_Flop d_ff_16 (.D(product[1]), .clk(CLK), .Q(product[0]));  // open: Qn, preset, reset
endmodule

module loader (
  input  rst,
  input  serialIn,
  input  clk,
  output DONE,
  output [15:0] parallelOut
);

  wire and_1_out, counter_1_carry, counter_2_carry, d_ff_1_q, not_1_out, not_2_out, not_3_out, or_1_out,
       or_2_out;
  wire [15:0] undriven;

  not not_1 (not_1_out, not_3_out);
  not not_2 (not_2_out, DONE);
  and and_1 (and_1_out, not_1_out, not_2_out);
  Counter #(.max('h8), .width(7)) counter_1 (
    .clr(rst), .up(1'b1), .count(not_3_out), .clk(clk), .carry(counter_1_carry));  // open: load, D, Q
  // Shift_Register #(.length(16)) shift_register_1: pin names not known; wires that end beside it: clk, rst, and_1_out, clk, serialIn, undriven[14], undriven[15], undriven[13], undriven[12], undriven[11], undriven[10], undriven[9], undriven[8], undriven[7], undriven[6], undriven[5], undriven[4]
  not not_3 (not_3_out, d_ff_1_q);
  D_Flip_Flop d_ff_1 (.D(or_1_out), .clk(clk), .Q(d_ff_1_q), .reset(rst));  // open: Qn, preset
  or or_1 (or_1_out, d_ff_1_q, counter_1_carry);
  Multiplexer #(.width(16)) multiplexer_1 (.in0({16{1'b0}}), .in1(undriven), .out(parallelOut), .sel(DONE));
  Counter #(.max('hf), .width(4)) counter_2 (
    .clr(rst), .up(1'b1), .count(and_1_out), .clk(clk), .carry(counter_2_carry));  // open: load, D, Q
  or or_2 (or_2_out, DONE, counter_2_carry);
  D_Flip_Flop d_ff_2 (.D(or_2_out), .clk(clk), .Q(DONE), .reset(rst));  // open: Qn, preset
endmodule
