// Logisim project mul.circ as structural Verilog: 3 circuits, main circuit main
module main (
  input  [7:0] X,
  input  in_2,
  input  R
);

  wire and_1_out, and_2_out, and_3_out, and_4_out, and_5_out, and_6_out, and_7_out, and_8_out, ciso_1_out_3,
       clk_out, csadd_1_sum, csadd_2_sum, csadd_3_sum, csadd_4_sum, csadd_5_sum, csadd_6_sum, csadd_7_sum,
       l_7_segment_display_driver_2dbc0fd3_1_p5, l_7_segment_display_driver_2dbc0fd3_1_p6,
       l_7_segment_display_driver_2dbc0fd3_1_p7, l_7_segment_display_driver_2dbc0fd3_1_p8,
       l_7_segment_display_driver_2dbc0fd3_1_p9, l_7_segment_display_driver_2dbc0fd3_1_p10,
       l_7_segment_display_driver_2dbc0fd3_1_p11, l_7_segment_display_driver_2dbc0fd3_2_p5,
       l_7_segment_display_driver_2dbc0fd3_2_p6, l_7_segment_display_driver_2dbc0fd3_2_p7,
       l_7_segment_display_driver_2dbc0fd3_2_p8, l_7_segment_display_driver_2dbc0fd3_2_p9,
       l_7_segment_display_driver_2dbc0fd3_2_p10, l_7_segment_display_driver_2dbc0fd3_2_p11,
       l_7_segment_display_driver_2dbc0fd3_3_p5, l_7_segment_display_driver_2dbc0fd3_3_p6,
       l_7_segment_display_driver_2dbc0fd3_3_p7, l_7_segment_display_driver_2dbc0fd3_3_p8,
       l_7_segment_display_driver_2dbc0fd3_3_p9, l_7_segment_display_driver_2dbc0fd3_3_p10,
       l_7_segment_display_driver_2dbc0fd3_3_p11, l_7_segment_display_driver_2dbc0fd3_4_p5,
       l_7_segment_display_driver_2dbc0fd3_4_p6, l_7_segment_display_driver_2dbc0fd3_4_p7,
       l_7_segment_display_driver_2dbc0fd3_4_p8, l_7_segment_display_driver_2dbc0fd3_4_p9,
       l_7_segment_display_driver_2dbc0fd3_4_p11, main_1_out_5;
  wire [15:0] l_7_segment_display_driver_2dbc0fd3_1_p4;

  Clock clk (.out(clk_out));
  ciso ciso_1 (.SI(in_2), .CLK(clk_out), .out_3(ciso_1_out_3));
  and and_1 (and_1_out, ciso_1_out_3, X[7]);
  theTCMP_main main_1 (.A(and_1_out), .R(R), .out_5(main_1_out_5), .in_2(clk_out));  // open: out_4
  and and_2 (and_2_out, ciso_1_out_3, X[6]);
  CSADD csadd_1 (.Y(and_2_out), .X(main_1_out_5), .R(R), .sum(csadd_1_sum), .clk(clk_out));  // open: FDHA
  and and_3 (and_3_out, ciso_1_out_3, X[5]);
  and and_4 (and_4_out, ciso_1_out_3, X[4]);
  CSADD csadd_2 (.Y(and_3_out), .X(csadd_1_sum), .R(R), .sum(csadd_2_sum), .clk(clk_out));  // open: FDHA
  and and_5 (and_5_out, ciso_1_out_3, X[3]);
  and and_6 (and_6_out, ciso_1_out_3, X[2]);
  CSADD csadd_3 (.Y(and_4_out), .X(csadd_2_sum), .R(R), .sum(csadd_3_sum), .clk(clk_out));  // open: FDHA
  and and_7 (and_7_out, ciso_1_out_3, X[1]);
  and and_8 (and_8_out, ciso_1_out_3, X[0]);
  CSADD csadd_4 (.Y(and_5_out), .X(csadd_3_sum), .R(R), .sum(csadd_4_sum), .clk(clk_out));  // open: FDHA
  CSADD csadd_5 (.Y(and_6_out), .X(csadd_4_sum), .R(R), .sum(csadd_5_sum), .clk(clk_out));  // open: FDHA
  CSADD csadd_6 (.Y(and_7_out), .X(csadd_5_sum), .R(R), .sum(csadd_6_sum), .clk(clk_out));  // open: FDHA
  // L_7_segment_display_driver_2dbc0fd3 l_7_segment_display_driver_2dbc0fd3_1: pin names not known; wires that end beside it: l_7_segment_display_driver_2dbc0fd3_1_p4[3], l_7_segment_display_driver_2dbc0fd3_1_p4[1], l_7_segment_display_driver_2dbc0fd3_1_p4[2], l_7_segment_display_driver_2dbc0fd3_1_p4[0], l_7_segment_display_driver_2dbc0fd3_1_p5, l_7_segment_display_driver_2dbc0fd3_1_p6, l_7_segment_display_driver_2dbc0fd3_1_p7, l_7_segment_display_driver_2dbc0fd3_1_p8, l_7_segment_display_driver_2dbc0fd3_1_p9, l_7_segment_display_driver_2dbc0fd3_1_p10, l_7_segment_display_driver_2dbc0fd3_1_p11
  // L_7_segment_display_driver_2dbc0fd3 l_7_segment_display_driver_2dbc0fd3_2: pin names not known; wires that end beside it: l_7_segment_display_driver_2dbc0fd3_1_p4[7], l_7_segment_display_driver_2dbc0fd3_1_p4[5], l_7_segment_display_driver_2dbc0fd3_1_p4[6], l_7_segment_display_driver_2dbc0fd3_1_p4[4], l_7_segment_display_driver_2dbc0fd3_2_p5, l_7_segment_display_driver_2dbc0fd3_2_p6, l_7_segment_display_driver_2dbc0fd3_2_p7, l_7_segment_display_driver_2dbc0fd3_2_p8, l_7_segment_display_driver_2dbc0fd3_2_p9, l_7_segment_display_driver_2dbc0fd3_2_p10, l_7_segment_display_driver_2dbc0fd3_2_p11
  // L_7_segment_display_driver_2dbc0fd3 l_7_segment_display_driver_2dbc0fd3_3: pin names not known; wires that end beside it: l_7_segment_display_driver_2dbc0fd3_1_p4[11], l_7_segment_display_driver_2dbc0fd3_1_p4[9], l_7_segment_display_driver_2dbc0fd3_1_p4[10], l_7_segment_display_driver_2dbc0fd3_1_p4[8], l_7_segment_display_driver_2dbc0fd3_3_p5, l_7_segment_display_driver_2dbc0fd3_3_p6, l_7_segment_display_driver_2dbc0fd3_3_p7, l_7_segment_display_driver_2dbc0fd3_3_p8, l_7_segment_display_driver_2dbc0fd3_3_p9, l_7_segment_display_driver_2dbc0fd3_3_p10, l_7_segment_display_driver_2dbc0fd3_3_p11
  // L_7_segment_display_driver_2dbc0fd3 l_7_segment_display_driver_2dbc0fd3_4: pin names not known; wires that end beside it: l_7_segment_display_driver_2dbc0fd3_1_p4[15], l_7_segment_display_driver_2dbc0fd3_1_p4[13], l_7_segment_display_driver_2dbc0fd3_1_p4[14], l_7_segment_display_driver_2dbc0fd3_1_p4[12], l_7_segment_display_driver_2dbc0fd3_4_p5, l_7_segment_display_driver_2dbc0fd3_4_p6, l_7_segment_display_driver_2dbc0fd3_4_p7, l_7_segment_display_driver_2dbc0fd3_4_p8, l_7_segment_display_driver_2dbc0fd3_4_p9, l_7_segment_display_driver_2dbc0fd3_4_p5, l_7_segment_display_driver_2dbc0fd3_4_p11
  _7_Segment_Display u_7_segment_display_1 (
    .g(l_7_segment_display_driver_2dbc0fd3_4_p11), .f(l_7_segment_display_driver_2dbc0fd3_4_p5),
    .a(l_7_segment_display_driver_2dbc0fd3_4_p5), .b(l_7_segment_display_driver_2dbc0fd3_4_p6),
    .e(l_7_segment_display_driver_2dbc0fd3_4_p9), .d(l_7_segment_display_driver_2dbc0fd3_4_p8),
    .c(l_7_segment_display_driver_2dbc0fd3_4_p7));  // open: dp
  CSADD csadd_7 (.Y(and_8_out), .X(csadd_6_sum), .R(R), .sum(csadd_7_sum), .clk(clk_out));  // open: FDHA
  _7_Segment_Display u_7_segment_display_2 (
    .g(l_7_segment_display_driver_2dbc0fd3_3_p11), .f(l_7_segment_display_driver_2dbc0fd3_3_p10),
    .a(l_7_segment_display_driver_2dbc0fd3_3_p5), .b(l_7_segment_display_driver_2dbc0fd3_3_p6),
    .e(l_7_segment_display_driver_2dbc0fd3_3_p9), .d(l_7_segment_display_driver_2dbc0fd3_3_p8),
    .c(l_7_segment_display_driver_2dbc0fd3_3_p7));  // open: dp
  sipo sipo_1 (.SI(csadd_7_sum), .CLK(clk_out), .product(l_7_segment_display_driver_2dbc0fd3_1_p4));
  _7_Segment_Display u_7_segment_display_3 (
    .g(l_7_segment_display_driver_2dbc0fd3_2_p11), .f(l_7_segment_display_driver_2dbc0fd3_2_p10),
    .a(l_7_segment_display_driver_2dbc0fd3_2_p5), .b(l_7_segment_display_driver_2dbc0fd3_2_p6),
    .e(l_7_segment_display_driver_2dbc0fd3_2_p9), .d(l_7_segment_display_driver_2dbc0fd3_2_p8),
    .c(l_7_segment_display_driver_2dbc0fd3_2_p7));  // open: dp
  _7_Segment_Display u_7_segment_display_4 (
    .g(l_7_segment_display_driver_2dbc0fd3_1_p11), .f(l_7_segment_display_driver_2dbc0fd3_1_p10),
    .a(l_7_segment_display_driver_2dbc0fd3_1_p5), .b(l_7_segment_display_driver_2dbc0fd3_1_p6),
    .e(l_7_segment_display_driver_2dbc0fd3_1_p9), .d(l_7_segment_display_driver_2dbc0fd3_1_p8),
    .c(l_7_segment_display_driver_2dbc0fd3_1_p7));  // open: dp
endmodule

module ciso (
  input  SI,
  input  CLK,
  output out_3
);

  wire d_ff_1_q, d_ff_2_q, d_ff_3_q, d_ff_4_q, d_ff_5_q, d_ff_6_q, d_ff_7_q;

  D_Flip_Flop d_ff_1 (.D(SI), .clk(CLK), .Q(d_ff_1_q));  // open: Qn, preset, reset
  D_Flip_Flop d_ff_2 (.D(d_ff_1_q), .clk(CLK), .Q(d_ff_2_q));  // open: Qn, preset, reset
  D_Flip_Flop d_ff_3 (.D(d_ff_2_q), .clk(CLK), .Q(d_ff_3_q));  // open: Qn, preset, reset
  D_Flip_Flop d_ff_4 (.D(d_ff_3_q), .clk(CLK), .Q(d_ff_4_q));  // open: Qn, preset, reset
  D_Flip_Flop d_ff_5 (.D(d_ff_4_q), .clk(CLK), .Q(d_ff_5_q));  // open: Qn, preset, reset
  D_Flip_Flop d_ff_6 (.D(d_ff_5_q), .clk(CLK), .Q(d_ff_6_q));  // open: Qn, preset, reset
  D_Flip_Flop d_ff_7 (.D(d_ff_6_q), .clk(CLK), .Q(d_ff_7_q));  // open: Qn, preset, reset
  D_Flip_Flop d_ff_8 (.D(d_ff_7_q), .clk(CLK), .Q(out_3));  // open: Qn, preset, reset
endmodule

module sipo (
  input  SI,
  input  CLK,
  output [15:0] product
);

  D_Flip_Flop d_ff_1 (.D(SI), .clk(CLK), .Q(product[15]));  // open: Qn, preset, reset
  D_Flip_Flop d_ff_2 (.D(product[15]), .clk(CLK), .Q(product[14]));  // open: Qn, preset, reset
  D_Flip_Flop d_ff_3 (.D(product[14]), .clk(CLK), .Q(product[13]));  // open: Qn, preset, reset
  D_Flip_Flop d_ff_4 (.D(product[13]), .clk(CLK), .Q(product[12]));  // open: Qn, preset, reset
  D_Flip_Flop d_ff_5 (.D(product[12]), .clk(CLK), .Q(product[11]));  // open: Qn, preset, reset
  D_Flip_Flop d_ff_6 (.D(product[11]), .clk(CLK), .Q(product[10]));  // open: Qn, preset, reset
  D_Flip_Flop d_ff_7 (.D(product[10]), .clk(CLK), .Q(product[9]));  // open: Qn, preset, reset
  D_Flip_Flop d_ff_8 (.D(product[9]), .clk(CLK), .Q(product[8]));  // open: Qn, preset, reset
  D_Flip_Flop d_ff_9 (.D(product[8]), .clk(CLK), .Q(product[7]));  // open: Qn, preset, reset
  D_Flip_Flop d_ff_10 (.D(product[7]), .clk(CLK), .Q(product[6]));  // open: Qn, preset, reset
  D_Flip_Flop d_ff_11 (.D(product[6]), .clk(CLK), .Q(product[5]));  // open: Qn, preset, reset
  D_Flip_Flop d_ff_12 (.D(product[5]), .clk(CLK), .Q(product[4]));  // open: Qn, preset, reset
  D_Flip_Flop d_ff_13 (.D(product[4]), .clk(CLK), .Q(product[3]));  // open: Qn, preset, reset
  D_Flip_Flop d_ff_14 (.D(product[3]), .clk(CLK), .Q(product[2]));  // open: Qn, preset, reset
  D_Flip_Flop d_ff_15 (.D(product[2]), .clk(CLK), .Q(product[1]));  // open: Qn, preset, reset
  D_Flip_Flop d_ff_16 (.D(product[1]), .clk(CLK), .Q(product[0]));  // open: Qn, preset, reset
endmodule
