// Logisim project theTCMP.circ as structural Verilog
module main (
  input  A,
  input  in_2,
  input  R,
  output out_4,
  output out_5
);

  wire d_ff_2_q, or_1_out, xor_1_out;

  and and_1 (out_4, A, d_ff_2_q);
  xor xor_1 (xor_1_out, A, d_ff_2_q);
  or or_1 (or_1_out, A, d_ff_2_q);
  D_Flip_Flop d_ff_1 (.D(xor_1_out), .clk(in_2), .Q(out_5), .reset(R));  // open: Qn, preset
  D_Flip_Flop d_ff_2 (.D(or_1_out), .clk(in_2), .Q(d_ff_2_q), .reset(R));  // open: Qn, preset
endmodule
